// Logisim project cpu.circ as structural Verilog: 5 circuits, main circuit main
module main (
  input  [31:0] INSTRUCTION,
  input  CLOCK,
  output [31:0] PROGRAM_COUNTER,
  output [31:0] ra,
  output [31:0] sp,
  output [31:0] t0,
  output [31:0] t1,
  output [31:0] t2,
  output [31:0] s0,
  output [31:0] s1,
  output [31:0] a0
);

  wire MemRW;
  wire [2:0] funct3;
  wire [3:0] ALUSel;
  wire [4:0] rd, rs1, rs2;
  wire [6:0] opcode;
  wire [11:0] imm;
  wire [31:0] ALUOut, immOut, MemData, multiplexer_1_out, multiplexer_2_out, multiplexer_3_out, PCPlus4,
       rs1Out, rs2Out, wb;

  Adder #(.width(32)) adder_1 (.a(PROGRAM_COUNTER), .b(32'h4), .out(PCPlus4));  // open: cin, cout
  Multiplexer #(.width(32), .enable("false")) multiplexer_1 (
    .in0(PCPlus4), .in1(ALUOut), .out(multiplexer_1_out), .sel(1'b0));
  Register #(.width(32)) PC (.D(multiplexer_1_out), .clk(CLOCK), .Q(PROGRAM_COUNTER));  // open: en, clr
  Decodery decodery_1 (
    .Instruction(INSTRUCTION), .clk(CLOCK), .opcode(opcode), .rd(rd), .funct3(funct3), .rs1(rs1), .rs2(rs2),
    .immI(imm));
  ImmGen immgen_1 (.ImmSel(1'b1), .imm(imm), .out_3(immOut));
  regfile_main RegFile (
    .rs2(rs2), .rd(rd), .Read_Data_1(rs1Out), .Read_Data_2(rs2Out), .ra(ra), .sp(sp), .t0(t0), .t1(t1),
    .t2(t2), .s0(s0), .s1(s1), .a0(a0), .rs1(rs1), .Write_Data(wb), .RegWEn(1'b1), .clk(CLOCK));
  BranchComp branchcomp_1 (.rs1(rs1Out), .rs2(rs2Out));  // open: BrUn, BrEq, BrLt
  Multiplexer #(.width(32), .enable("false")) multiplexer_2 (
    .in0(rs1Out), .in1(PROGRAM_COUNTER), .out(multiplexer_2_out), .sel(1'b0));
  Multiplexer #(.width(32), .enable("false")) multiplexer_3 (
    .in0(rs2Out), .in1(immOut), .out(multiplexer_3_out), .sel(1'b1));
  alu alu_1 (.B(multiplexer_3_out), .Result(ALUOut), .A(multiplexer_2_out), .ALUSel(ALUSel));
  // mem_main DMEM: pin names not known; wires that end beside it: ALUOut, rs2Out, CLOCK, MemRW, MemData
  Multiplexer #(.select(2), .width(32), .enable("false")) multiplexer_4 (
    .in0(PCPlus4), .in1(ALUOut), .in3(MemData), .out(wb), .sel(2'b01));  // open: in2

  // Other names for the same wires on the sheet: clk = CLOCK

  // Notes on the sheet:
  //   Output
  //   IMEM (do **NOT** move this)
  //   Inputs
  //   Inputs/Outputs for testing. Do **NOT** move these.
endmodule

module ImmGen (
  input  ImmSel,
  input  [11:0] imm,
  output [31:0] out_3
);

  wire bitselector_1_out;
  wire [31:0] and_1_out, bit_extender_1_out;

  BitSelector #(.width(12)) bitselector_1 (.in(imm), .out(bitselector_1_out), .sel(4'b1011));
  assign bit_extender_1_out = {{20{imm[11]}}, imm};  // Bit_Extender bit_extender_1
  Multiplexer #(.width(32), .enable("false")) multiplexer_1 (
    .in0(bit_extender_1_out), .in1(and_1_out), .out(out_3), .sel(bitselector_1_out));
  assign and_1_out = {32{1'b1}} & bit_extender_1_out;  // AND_Gate and_1, 32 bits wide
endmodule

module Decodery (
  input  [31:0] Instruction,
  input  clk,
  output [6:0] opcode,
  output [4:0] rd,
  output [2:0] funct3,
  output [4:0] rs1,
  output [4:0] rs2,
  output [11:0] immI
);

  Register #(.width(32)) register_1 (.D(Instruction), .clk(clk), .Q({immI, rs1, funct3, rd, opcode}));  // open: en, clr

  assign rs2 = immI[4:0];
endmodule

module Control (
  input  [6:0] opcode,
  input  [2:0] funct3,
  input  [5:0] BrEq,
  input  [5:0] BrLt,
  output PCSel,
  output RegWEn,
  output ImmSel,
  output BrUn,
  output BSel,
  output ASel,
  output [4:0] ALUSel,
  output MemRW,
  output WBSel
);
endmodule

module BranchComp (
  input  [31:0] rs1,
  input  [31:0] rs2,
  input  [5:0] BrUn,
  output BrEq,
  output BrLt
);
endmodule
